// Logisim project EdgeComputer.circ as structural Verilog: 6 circuits, main circuit main
module main (
  input  RST,
  input  CLK,
  input  [1:0] TLB_INDEX,
  input  RD,
  input  WR,
  input  [15:0] DATA,
  input  [3:0] PID,
  input  [23:0] ADDR,
  input  TLB_DISABLE,
  output [23:0] out_10
);

  wire decoder_1_out1, decoder_1_out2, decoder_1_out3;
  wire [3:0] register_1_q;
  wire [11:0] tlb_matrix_1_addr_out;

  Decoder #(.select(2), .enable("false")) decoder_1 (
    .out1(decoder_1_out1), .out2(decoder_1_out2), .out3(decoder_1_out3), .sel(TLB_INDEX));  // open: out0
  Register #(.width(4)) register_1 (.D(DATA[3:0]), .en(decoder_1_out1), .Q(register_1_q), .clk(CLK), .clr(RST));
  TLB_Matrix tlb_matrix_1 (
    .ADDR(ADDR[23:12]), .PID(PID), .DATA(DATA), .RST(RST), .WFLAG(decoder_1_out2), .WBANK(decoder_1_out3),
    .RD(RD), .WR(WR), .CLK(CLK), .INDEX(register_1_q), .ADDR_OUT(tlb_matrix_1_addr_out));
  Multiplexer #(.width(12), .enable("false")) multiplexer_1 (
    .in0(tlb_matrix_1_addr_out), .in1(ADDR[11:0]), .out(out_10[23:12]), .sel(TLB_DISABLE));

  assign out_10[11:0] = ADDR[23:12];
endmodule

module SN74172_Register (
  input  [15:0] D0,
  input  [15:0] D1,
  input  WR0,
  input  WR1,
  input  CLK,
  output [15:0] Q
);

  wire or_1_out;
  wire [15:0] and_1_out, pull_resistor_1_node, pull_resistor_2_node;

  Pull_Resistor #(.pull(1)) pull_resistor_1 (.node(pull_resistor_1_node));
  Pull_Resistor #(.pull(1)) pull_resistor_2 (.node(pull_resistor_2_node));
  assign pull_resistor_2_node = WR0 ? D0 : 16'bz;  // Controlled_Buffer controlled_buffer_1
  assign pull_resistor_1_node = WR1 ? D1 : 16'bz;  // Controlled_Buffer controlled_buffer_2
  assign and_1_out = pull_resistor_2_node & pull_resistor_1_node;  // AND_Gate and_1, 16 bits wide
  or or_1 (or_1_out, WR0, WR1);
  Register #(.width(16)) register_1 (.D(and_1_out), .en(or_1_out), .Q(Q), .clk(CLK));  // open: clr
endmodule

module DualPort_Reg_File (
  input  CLK,
  input  [15:0] D0,
  input  [15:0] D1,
  input  [2:0] W0,
  input  [2:0] R0,
  input  [2:0] WR1,
  input  nWE0,
  input  nWE1,
  input  nRE0,
  input  nRE1,
  output [15:0] Q0,
  output [15:0] Q1
);

  wire decoder_1_out0, decoder_1_out1, decoder_1_out2, decoder_1_out3, decoder_1_out4, decoder_1_out5,
       decoder_1_out6, decoder_1_out7, decoder_2_out0, decoder_2_out1, decoder_2_out2, decoder_2_out3,
       decoder_2_out4, decoder_2_out5, decoder_2_out6, decoder_2_out7, not_1_out, not_2_out, not_3_out,
       not_4_out;
  wire [15:0] sn74172_register_1_q, sn74172_register_2_q, sn74172_register_3_q, sn74172_register_4_q,
       sn74172_register_5_q, sn74172_register_6_q, sn74172_register_7_q, sn74172_register_8_q;

  not not_1 (not_1_out, nWE0);
  not not_2 (not_2_out, nWE1);
  not not_3 (not_3_out, nRE0);
  not not_4 (not_4_out, nRE1);
  Decoder #(.select(3), .disabled(0)) decoder_1 (
    .out0(decoder_1_out0), .out1(decoder_1_out1), .out2(decoder_1_out2), .out3(decoder_1_out3),
    .out4(decoder_1_out4), .out5(decoder_1_out5), .out6(decoder_1_out6), .out7(decoder_1_out7), .sel(W0),
    .en(not_1_out));
  Decoder #(.select(3), .disabled(0)) decoder_2 (
    .out0(decoder_2_out0), .out1(decoder_2_out1), .out2(decoder_2_out2), .out3(decoder_2_out3),
    .out4(decoder_2_out4), .out5(decoder_2_out5), .out6(decoder_2_out6), .out7(decoder_2_out7), .sel(WR1),
    .en(not_2_out));
  SN74172_Register sn74172_register_1 (
    .D0(D0), .D1(D1), .WR0(decoder_1_out0), .WR1(decoder_2_out0), .CLK(CLK), .Q(sn74172_register_1_q));
  SN74172_Register sn74172_register_2 (
    .D0(D0), .D1(D1), .WR0(decoder_1_out1), .WR1(decoder_2_out1), .CLK(CLK), .Q(sn74172_register_2_q));
  SN74172_Register sn74172_register_3 (
    .D0(D0), .D1(D1), .WR0(decoder_1_out2), .WR1(decoder_2_out2), .CLK(CLK), .Q(sn74172_register_3_q));
  SN74172_Register sn74172_register_4 (
    .D0(D0), .D1(D1), .WR0(decoder_1_out3), .WR1(decoder_2_out3), .CLK(CLK), .Q(sn74172_register_4_q));
  SN74172_Register sn74172_register_5 (
    .D0(D0), .D1(D1), .WR0(decoder_1_out4), .WR1(decoder_2_out4), .CLK(CLK), .Q(sn74172_register_5_q));
  SN74172_Register sn74172_register_6 (
    .D0(D0), .D1(D1), .WR0(decoder_1_out5), .WR1(decoder_2_out5), .CLK(CLK), .Q(sn74172_register_6_q));
  SN74172_Register sn74172_register_7 (
    .D0(D0), .D1(D1), .WR0(decoder_1_out6), .WR1(decoder_2_out6), .CLK(CLK), .Q(sn74172_register_7_q));
  SN74172_Register sn74172_register_8 (
    .D0(D0), .D1(D1), .WR0(decoder_1_out7), .WR1(decoder_2_out7), .CLK(CLK), .Q(sn74172_register_8_q));
  Multiplexer #(.select(3), .width(16)) multiplexer_1 (
    .in0(sn74172_register_1_q), .in1(sn74172_register_2_q), .in2(sn74172_register_3_q),
    .in3(sn74172_register_4_q), .in4(sn74172_register_5_q), .in5(sn74172_register_6_q),
    .in6(sn74172_register_7_q), .in7(sn74172_register_8_q), .out(Q1), .sel(WR1), .en(not_4_out));
  Multiplexer #(.select(3), .width(16)) multiplexer_2 (
    .in0(sn74172_register_1_q), .in1(sn74172_register_2_q), .in2(sn74172_register_3_q),
    .in3(sn74172_register_4_q), .in4(sn74172_register_5_q), .in5(sn74172_register_6_q),
    .in6(sn74172_register_7_q), .in7(sn74172_register_8_q), .out(Q0), .sel(R0), .en(not_3_out));
endmodule

module Immediate (
  input  invert,
  input  decr,
  input  [3:0] \bit ,
  output [15:0] out_4
);

  wire not_1_out, not_2_out;
  wire [15:0] decoder_1_out0, subtractor_1_out;

  not not_1 (not_1_out, decr);
  Decoder #(.select(4), .disabled(0), .enable("false")) decoder_1 (
    .out0(decoder_1_out0[0]), .out1(decoder_1_out0[1]), .out2(decoder_1_out0[2]), .out3(decoder_1_out0[3]),
    .out4(decoder_1_out0[4]), .out5(decoder_1_out0[5]), .out6(decoder_1_out0[6]), .out7(decoder_1_out0[7]),
    .out8(decoder_1_out0[8]), .out9(decoder_1_out0[9]), .out10(decoder_1_out0[10]),
    .out11(decoder_1_out0[11]), .out12(decoder_1_out0[12]), .out13(decoder_1_out0[13]),
    .out14(decoder_1_out0[14]), .out15(decoder_1_out0[15]), .sel(\bit ));
  Subtractor #(.width(16)) subtractor_1 (
    .a(decoder_1_out0), .b({16{1'b0}}), .out(subtractor_1_out), .bin(not_1_out));  // open: bout
  not not_2 (not_2_out, invert);
  assign out_4 = not_2_out ? subtractor_1_out : 16'bz;  // Controlled_Buffer controlled_buffer_1
  assign out_4 = invert ? ~subtractor_1_out : 16'bz;  // Controlled_Inverter controlled_inverter_1
endmodule

module TLB_Cell (
  input  CLK,
  input  WR,
  input  RD,
  input  SEL,
  input  WBANK,
  input  WFLAG,
  input  RST,
  input  [15:0] DATA,
  input  [3:0] PID,
  input  [11:0] ADDR,
  input  PREVIOUS,
  output ACTIVE,
  output [11:0] ADDR_OUT
);

  wire and_1_out, and_2_out, and_3_out, and_4_out, comparator_1_eq, not_1_out, or_1_out;
  wire [11:0] controlled_buffer_1_out;
  wire [15:0] register_1_q, register_2_q;

  and and_1 (and_1_out, SEL, WBANK);
  and and_2 (and_2_out, WFLAG, SEL);
  Register #(.width(16)) register_1 (.D(DATA), .en(and_1_out), .Q(register_1_q), .clk(CLK), .clr(RST));
  Register #(.width(16)) register_2 (.D(DATA), .en(and_2_out), .Q(register_2_q), .clk(CLK), .clr(RST));
  Comparator #(.width(16)) comparator_1 (.a(register_1_q), .b({ADDR, PID}), .eq(comparator_1_eq));  // open: gt, lt
  and and_3 (and_3_out, register_2_q[0], WR);
  and and_4 (and_4_out, RD, register_2_q[1]);
  or or_1 (or_1_out, and_3_out, and_4_out);
  and and_5 (ACTIVE, comparator_1_eq, register_2_q[2]);
  not not_1 (not_1_out, PREVIOUS);
  assign controlled_buffer_1_out = ACTIVE ? register_2_q[15:4] : 12'bz;  // Controlled_Buffer controlled_buffer_1
  assign ADDR_OUT = not_1_out ? controlled_buffer_1_out : 12'bz;  // Controlled_Buffer controlled_buffer_2

  // Notes on the sheet:
  //   PREVIOUS: pull=down
endmodule

module TLB_Matrix (
  input  [11:0] ADDR,
  input  [3:0] PID,
  input  [15:0] DATA,
  input  RST,
  input  WFLAG,
  input  WBANK,
  input  RD,
  input  WR,
  input  CLK,
  input  [3:0] INDEX,
  output [11:0] ADDR_OUT
);

  wire decoder_1_out0, decoder_1_out1, decoder_1_out2, decoder_1_out3, decoder_1_out4, decoder_1_out5,
       decoder_1_out6, decoder_1_out7, decoder_1_out8, decoder_1_out9, decoder_1_out10, decoder_1_out11,
       decoder_1_out12, decoder_1_out13, decoder_1_out14, decoder_1_out15, tlb_cell_1_active,
       tlb_cell_2_active, tlb_cell_3_active, tlb_cell_5_active, tlb_cell_6_active, tlb_cell_7_active,
       tlb_cell_9_active, tlb_cell_10_active, tlb_cell_11_active, tlb_cell_13_active, tlb_cell_14_active,
       tlb_cell_15_active;
  wire [11:0] tlb_cell_1_addr_out, tlb_cell_5_addr_out;

  Decoder #(.select(4), .enable("false")) decoder_1 (
    .out0(decoder_1_out0), .out1(decoder_1_out1), .out2(decoder_1_out2), .out3(decoder_1_out3),
    .out4(decoder_1_out4), .out5(decoder_1_out5), .out6(decoder_1_out6), .out7(decoder_1_out7),
    .out8(decoder_1_out8), .out9(decoder_1_out9), .out10(decoder_1_out10), .out11(decoder_1_out11),
    .out12(decoder_1_out12), .out13(decoder_1_out13), .out14(decoder_1_out14), .out15(decoder_1_out15),
    .sel(INDEX));
  TLB_Cell tlb_cell_1 (
    .CLK(CLK), .WR(WR), .RD(RD), .SEL(decoder_1_out3), .WBANK(WBANK), .WFLAG(WFLAG), .RST(RST), .DATA(DATA),
    .PID(PID), .ADDR(ADDR), .ACTIVE(tlb_cell_1_active), .ADDR_OUT(tlb_cell_1_addr_out));  // open: PREVIOUS
  TLB_Cell tlb_cell_2 (
    .SEL(decoder_1_out2), .PREVIOUS(tlb_cell_1_active), .ACTIVE(tlb_cell_2_active),
    .ADDR_OUT(tlb_cell_1_addr_out));  // open: CLK, WR, RD, WBANK, WFLAG, RST, DATA, PID, ADDR
  TLB_Cell tlb_cell_3 (
    .SEL(decoder_1_out1), .PREVIOUS(tlb_cell_2_active), .ACTIVE(tlb_cell_3_active),
    .ADDR_OUT(tlb_cell_1_addr_out));  // open: CLK, WR, RD, WBANK, WFLAG, RST, DATA, PID, ADDR
  TLB_Cell tlb_cell_4 (
    .SEL(decoder_1_out0), .PREVIOUS(tlb_cell_3_active), .ADDR_OUT(tlb_cell_1_addr_out));  // open: CLK, WR, RD, WBANK, WFLAG, RST, DATA, PID, ADDR, ACTIVE
  TLB_Cell tlb_cell_5 (
    .CLK(CLK), .WR(WR), .RD(RD), .SEL(decoder_1_out4), .WBANK(WBANK), .WFLAG(WFLAG), .RST(RST), .DATA(DATA),
    .PID(PID), .ADDR(ADDR), .ACTIVE(tlb_cell_5_active), .ADDR_OUT(tlb_cell_5_addr_out));  // open: PREVIOUS
  TLB_Cell tlb_cell_6 (
    .SEL(decoder_1_out5), .PREVIOUS(tlb_cell_5_active), .ACTIVE(tlb_cell_6_active),
    .ADDR_OUT(tlb_cell_5_addr_out));  // open: CLK, WR, RD, WBANK, WFLAG, RST, DATA, PID, ADDR
  TLB_Cell tlb_cell_7 (
    .SEL(decoder_1_out6), .PREVIOUS(tlb_cell_6_active), .ACTIVE(tlb_cell_7_active),
    .ADDR_OUT(tlb_cell_5_addr_out));  // open: CLK, WR, RD, WBANK, WFLAG, RST, DATA, PID, ADDR
  TLB_Cell tlb_cell_8 (
    .SEL(decoder_1_out7), .PREVIOUS(tlb_cell_7_active), .ADDR_OUT(tlb_cell_5_addr_out));  // open: CLK, WR, RD, WBANK, WFLAG, RST, DATA, PID, ADDR, ACTIVE
  TLB_Cell tlb_cell_9 (
    .CLK(CLK), .WR(WR), .RD(RD), .SEL(decoder_1_out8), .WBANK(WBANK), .WFLAG(WFLAG), .RST(RST), .DATA(DATA),
    .PID(PID), .ADDR(ADDR), .ACTIVE(tlb_cell_9_active));  // open: PREVIOUS, ADDR_OUT
  TLB_Cell tlb_cell_10 (
    .SEL(decoder_1_out9), .PREVIOUS(tlb_cell_9_active), .ACTIVE(tlb_cell_10_active));  // open: CLK, WR, RD, WBANK, WFLAG, RST, DATA, PID, ADDR, ADDR_OUT
  TLB_Cell tlb_cell_11 (
    .SEL(decoder_1_out10), .PREVIOUS(tlb_cell_10_active), .ACTIVE(tlb_cell_11_active));  // open: CLK, WR, RD, WBANK, WFLAG, RST, DATA, PID, ADDR, ADDR_OUT
  TLB_Cell tlb_cell_12 (
    .SEL(decoder_1_out11), .PREVIOUS(tlb_cell_11_active));  // open: CLK, WR, RD, WBANK, WFLAG, RST, DATA, PID, ADDR, ACTIVE, ADDR_OUT
  TLB_Cell tlb_cell_13 (
    .CLK(CLK), .WR(WR), .RD(RD), .SEL(decoder_1_out12), .WBANK(WBANK), .WFLAG(WFLAG), .RST(RST), .DATA(DATA),
    .PID(PID), .ADDR(ADDR), .ACTIVE(tlb_cell_13_active));  // open: PREVIOUS, ADDR_OUT
  TLB_Cell tlb_cell_14 (
    .SEL(decoder_1_out13), .PREVIOUS(tlb_cell_13_active), .ACTIVE(tlb_cell_14_active));  // open: CLK, WR, RD, WBANK, WFLAG, RST, DATA, PID, ADDR, ADDR_OUT
  TLB_Cell tlb_cell_15 (
    .SEL(decoder_1_out14), .PREVIOUS(tlb_cell_14_active), .ACTIVE(tlb_cell_15_active));  // open: CLK, WR, RD, WBANK, WFLAG, RST, DATA, PID, ADDR, ADDR_OUT
  TLB_Cell tlb_cell_16 (
    .SEL(decoder_1_out15), .PREVIOUS(tlb_cell_15_active));  // open: CLK, WR, RD, WBANK, WFLAG, RST, DATA, PID, ADDR, ACTIVE, ADDR_OUT
endmodule
